// Digital circuit comp.dig as structural Verilog
module comp (
  input  [7:0] A,
  input  [7:0] B,
  output A_lt_B,
  output A_eq_B,
  output A_gt_B
);

  wire comp_1bit_2__0__eq, comp_1bit_2__0__gt, comp_1bit_2__0__lt, comp_1bit_3__0__eq, comp_1bit_3__0__gt,
       comp_1bit_3__0__lt, comp_1bit_4__0__eq, comp_1bit_4__0__gt, comp_1bit_4__0__lt, comp_1bit_5__0__eq,
       comp_1bit_5__0__gt, comp_1bit_5__0__lt, comp_1bit_6__0__eq, comp_1bit_6__0__gt, comp_1bit_6__0__lt,
       comp_1bit_7__0__eq, comp_1bit_7__0__gt, comp_1bit_7__0__lt, comp_meio_1__0__eq, comp_meio_1_o__gt,
       comp_meio_1_o__lt;

  comp_1bit comp_1bit_1 (
    .A(A[7]), .B(B[7]), .I__lt(comp_1bit_2__0__lt), .I__eq(comp_1bit_2__0__eq), .I__gt(comp_1bit_2__0__gt),
    ._0__lt(A_lt_B), ._0__eq(A_eq_B), ._0__gt(A_gt_B));
  comp_1bit comp_1bit_2 (
    .A(A[6]), .B(B[6]), .I__lt(comp_1bit_3__0__lt), .I__eq(comp_1bit_3__0__eq), .I__gt(comp_1bit_3__0__gt),
    ._0__lt(comp_1bit_2__0__lt), ._0__eq(comp_1bit_2__0__eq), ._0__gt(comp_1bit_2__0__gt));
  comp_1bit comp_1bit_3 (
    .A(A[5]), .B(B[5]), .I__lt(comp_1bit_4__0__lt), .I__eq(comp_1bit_4__0__eq), .I__gt(comp_1bit_4__0__gt),
    ._0__lt(comp_1bit_3__0__lt), ._0__eq(comp_1bit_3__0__eq), ._0__gt(comp_1bit_3__0__gt));
  comp_1bit comp_1bit_4 (
    .A(A[4]), .B(B[4]), .I__lt(comp_1bit_5__0__lt), .I__eq(comp_1bit_5__0__eq), .I__gt(comp_1bit_5__0__gt),
    ._0__lt(comp_1bit_4__0__lt), ._0__eq(comp_1bit_4__0__eq), ._0__gt(comp_1bit_4__0__gt));
  comp_1bit comp_1bit_5 (
    .A(A[3]), .B(B[3]), .I__lt(comp_1bit_6__0__lt), .I__eq(comp_1bit_6__0__eq), .I__gt(comp_1bit_6__0__gt),
    ._0__lt(comp_1bit_5__0__lt), ._0__eq(comp_1bit_5__0__eq), ._0__gt(comp_1bit_5__0__gt));
  comp_1bit comp_1bit_6 (
    .A(A[2]), .B(B[2]), .I__lt(comp_1bit_7__0__lt), .I__eq(comp_1bit_7__0__eq), .I__gt(comp_1bit_7__0__gt),
    ._0__lt(comp_1bit_6__0__lt), ._0__eq(comp_1bit_6__0__eq), ._0__gt(comp_1bit_6__0__gt));
  comp_1bit comp_1bit_7 (
    .A(A[1]), .B(B[1]), .I__lt(comp_meio_1_o__lt), .I__eq(comp_meio_1__0__eq), .I__gt(comp_meio_1_o__gt),
    ._0__lt(comp_1bit_7__0__lt), ._0__eq(comp_1bit_7__0__eq), ._0__gt(comp_1bit_7__0__gt));
  comp_meio comp_meio_1 (
    .A(A[0]), .B(B[0]), .O__lt(comp_meio_1_o__lt), .O__gt(comp_meio_1_o__gt), ._0__eq(comp_meio_1__0__eq));
endmodule
