// Digital circuit comp_1bit.dig as structural Verilog
module comp_1bit (
  input  A,
  input  B,
  input  I__lt,
  input  I__eq,
  input  I__gt,
  output _0__lt,
  output _0__eq,
  output _0__gt
);

  wire and_1_out, and_2_out, and_3_out, and_4_out, and_5_out, and_6_out, and_7_out, and_8_out, not_1_out,
       not_2_out;

  not not_1 (not_1_out, A);
  not not_2 (not_2_out, B);
  and and_1 (and_1_out, not_1_out, B);
  and and_2 (and_2_out, not_1_out, I__lt);
  and and_3 (and_3_out, B, I__lt);
  and and_4 (and_4_out, not_1_out, not_2_out, I__eq);
  and and_5 (and_5_out, A, B, I__eq);
  and and_6 (and_6_out, A, not_2_out);
  and and_7 (and_7_out, not_2_out, I__gt);
  and and_8 (and_8_out, A, I__gt);
  or or_1 (_0__lt, and_1_out, and_2_out, and_3_out);
  or or_2 (_0__eq, and_4_out, and_5_out);
  or or_3 (_0__gt, and_6_out, and_7_out, and_8_out);
endmodule
