// Digital circuit multiplicador.dig as structural Verilog
module multiplicador (
  input  [7:0] A,
  input  [7:0] B,
  output [7:0] Out
);

  wire and_1_out, and_2_out, and_3_out, and_4_out, and_5_out, and_6_out, and_7_out, and_8_out, and_9_out,
       and_10_out, and_11_out, and_12_out, and_13_out, and_14_out, and_15_out, fa_2_cout, fa_2_s, fa_3_cout,
       fa_4_cout, fa_4_s, fa_5_cout, fa_5_s, fa_6_cout, fa_7_cout, fa_7_s, fa_8_cout, fa_9_cout, fa_9_s,
       fa_10_cout, fa_11_cout, fa_11_s, fa_12_cout;

  and and_1 (and_1_out, B[3], A[3]);
  fa fa_1 (.A(fa_3_cout), .B(fa_2_cout), .Cin(and_1_out), .Cout(Out[7]), .S(Out[6]));
  and and_2 (and_2_out, B[3], A[2]);
  fa fa_2 (.A(fa_5_cout), .B(and_3_out), .Cin(and_2_out), .Cout(fa_2_cout), .S(fa_2_s));
  fa fa_3 (.A(fa_6_cout), .B(fa_4_cout), .Cin(fa_2_s), .Cout(fa_3_cout), .S(Out[5]));
  and and_3 (and_3_out, B[2], A[3]);
  and and_4 (and_4_out, B[3], A[1]);
  fa fa_4 (.A(fa_7_cout), .B(fa_5_s), .Cin(and_4_out), .Cout(fa_4_cout), .S(fa_4_s));
  and and_5 (and_5_out, B[2], A[2]);
  and and_6 (and_6_out, B[1], A[3]);
  fa fa_5 (.A(fa_9_cout), .B(and_6_out), .Cin(and_5_out), .Cout(fa_5_cout), .S(fa_5_s));
  fa fa_6 (.A(fa_4_s), .B(fa_8_cout), .Cin(1'b0), .Cout(fa_6_cout), .S(Out[4]));
  and and_7 (and_7_out, B[3], A[0]);
  fa fa_7 (.A(fa_10_cout), .B(and_8_out), .Cin(fa_9_s), .Cout(fa_7_cout), .S(fa_7_s));
  and and_8 (and_8_out, B[2], A[1]);
  and and_9 (and_9_out, B[1], A[2]);
  fa fa_8 (.A(fa_7_s), .B(and_7_out), .Cin(1'b0), .Cout(fa_8_cout), .S(Out[3]));
  and and_10 (and_10_out, B[0], A[3]);
  fa fa_9 (.A(fa_11_cout), .B(and_10_out), .Cin(and_9_out), .Cout(fa_9_cout), .S(fa_9_s));
  fa fa_10 (.A(fa_11_s), .B(and_11_out), .Cin(1'b0), .Cout(fa_10_cout), .S(Out[2]));
  and and_11 (and_11_out, B[2], A[0]);
  and and_12 (and_12_out, B[1], A[1]);
  and and_13 (and_13_out, B[0], A[2]);
  fa fa_11 (.A(fa_12_cout), .B(and_13_out), .Cin(and_12_out), .Cout(fa_11_cout), .S(fa_11_s));
  and and_14 (and_14_out, B[1], A[0]);
  and and_15 (and_15_out, B[0], A[1]);
  fa fa_12 (.A(and_15_out), .B(and_14_out), .Cin(1'b0), .Cout(fa_12_cout), .S(Out[1]));
  and and_16 (Out[0], B[0], A[0]);
endmodule
