// Digital circuit regs.dig as structural Verilog
module regs (
  input  [7:0] A,
  input  C,
  output [7:0] Out
);

  D_FF d_ff_1 (.D(A[0]), .C(C), .Q(Out[0]));  // open: nQ
  D_FF d_ff_2 (.D(A[1]), .C(C), .Q(Out[1]));  // open: nQ
  D_FF d_ff_3 (.D(A[2]), .C(C), .Q(Out[2]));  // open: nQ
  D_FF d_ff_4 (.D(A[3]), .C(C), .Q(Out[3]));  // open: nQ
  D_FF d_ff_5 (.D(A[4]), .C(C), .Q(Out[4]));  // open: nQ
  D_FF d_ff_6 (.D(A[5]), .C(C), .Q(Out[5]));  // open: nQ
  D_FF d_ff_7 (.D(A[6]), .C(C), .Q(Out[6]));  // open: nQ
  D_FF d_ff_8 (.D(A[7]), .C(C), .Q(Out[7]));  // open: nQ
endmodule
