// Digital circuit result.dig as structural Verilog
module result (
  input  [7:0] in_1,
  input  [7:0] in_2,
  input  [7:0] A,
  input  [7:0] B,
  input  [7:0] A_2,
  input  [7:0] B_2,
  input  C,
  input  [7:0] _0,
  input  [7:0] A_3,
  input  [7:0] B_3,
  input  [2:0] E,
  input  [7:0] A_4,
  input  [7:0] B_4,
  input  c_2
);

  wire button_1_out, comp_1_a_eq_b, comp_1_a_gt_b, comp_1_a_lt_b, comp_2_a_eq_b, comp_2_a_gt_b, comp_2_a_lt_b;
  wire [3:0] bit_shift_1_p3, multiplicador_1_out, multiplicador_1_out_2, sub_1_p3, sub_1_p3_2, sum_1_p3,
       sum_1_p3_2;
  wire [7:0] bit_shift_2_p3, multiplexer_1_out, multiplicador_2_out, regs_1_out, sub_2_p3, sum_2_p3;
  wire [7:4] bit_shift_1_p3_2;

  // sum sum_1: pin names not known; wires that end beside it: in_1, in_2, {sum_1_p3_2, sum_1_p3}
  // sub sub_1: pin names not known; wires that end beside it: A, B, {sub_1_p3_2, sub_1_p3}
  comp comp_1 (.A(A_2), .B(B_2), .A_lt_B(comp_1_a_lt_b), .A_eq_B(comp_1_a_eq_b), .A_gt_B(comp_1_a_gt_b));
  // bit_shift bit_shift_1: pin names not known; wires that end beside it: C, _0, {bit_shift_1_p3_2, bit_shift_1_p3}
  multiplicador multiplicador_1 (.A(A_3), .B(B_3), .Out({multiplicador_1_out_2, multiplicador_1_out}));
  Seven_Seg_Hex seven_seg_hex_1 (.d(bit_shift_1_p3_2), .dp(1'b0));
  Seven_Seg_Hex seven_seg_hex_2 (.d(multiplicador_1_out_2), .dp(1'b0));
  Seven_Seg_Hex seven_seg_hex_3 (.d(sum_1_p3), .dp(1'b0));
  Seven_Seg_Hex seven_seg_hex_4 (.d(sub_1_p3), .dp(1'b0));
  LED led_1 (.in(comp_1_a_lt_b));
  Seven_Seg_Hex seven_seg_hex_5 (.d(bit_shift_1_p3), .dp(1'b0));
  Seven_Seg_Hex seven_seg_hex_6 (.d(sum_1_p3_2), .dp(1'b0));
  Seven_Seg_Hex seven_seg_hex_7 (.d(sub_1_p3_2), .dp(1'b0));
  LED led_2 (.in(comp_1_a_eq_b));
  LED led_3 (.in(comp_1_a_gt_b));
  Seven_Seg_Hex seven_seg_hex_8 (.d(multiplicador_1_out), .dp(1'b0));
  // sum sum_2: pin names not known; wires that end beside it: A_4, B_4, sum_2_p3
  // sub sub_2: pin names not known; wires that end beside it: A_4, B_4, sub_2_p3
  multiplicador multiplicador_2 (.A(A_4), .B(B_4), .Out(multiplicador_2_out));
  // bit_shift bit_shift_2: pin names not known; wires that end beside it: c_2, A_4, bit_shift_2_p3
  comp comp_2 (.A(A_4), .B(B_4), .A_lt_B(comp_2_a_lt_b), .A_eq_B(comp_2_a_eq_b), .A_gt_B(comp_2_a_gt_b));
  LED led_4 (.in(comp_2_a_lt_b));
  LED led_5 (.in(comp_2_a_eq_b));
  LED led_6 (.in(comp_2_a_gt_b));
  Multiplexer #(.Selector_Bits(3), .Bits(8)) multiplexer_1 (
    .sel(E), .in_0(sum_2_p3), .in_1(sub_2_p3), .in_2(multiplicador_2_out), .in_3(bit_shift_2_p3),
    .in_4({8{1'b0}}), .in_5({8{1'b0}}), .in_6({8{1'b0}}), .in_7({8{1'b0}}), .out(multiplexer_1_out));
  Button button_1 (.out(button_1_out));
  regs regs_1 (.A(multiplexer_1_out), .C(button_1_out), .Out(regs_1_out));
  Seven_Seg_Hex seven_seg_hex_9 (.d(regs_1_out[7:4]), .dp(1'b0));
  Seven_Seg_Hex seven_seg_hex_10 (.d(regs_1_out[3:0]), .dp(1'b0));
endmodule
