// Digital circuit sa.dig as structural Verilog
module sa (
  input  A,
  input  B,
  input  IN,
  output Diff,
  output OUT
);

  wire and_1_out, and_2_out, and_3_out, xor_1_out;

  xor xor_1 (xor_1_out, A, B);
  and and_1 (and_1_out, A, IN);
  and and_2 (and_2_out, A, ~B);  // And
  and and_3 (and_3_out, IN, ~B);  // And
  xor xor_2 (Diff, xor_1_out, IN);
  or or_1 (OUT, and_1_out, and_2_out, and_3_out);
endmodule
