// Digital circuit sub.dig as structural Verilog
module sub (
  input  [7:0] A,
  input  [7:0] B,
  output [7:0] S
);

  wire sa_2_out, sa_3_out, sa_4_out, sa_5_out, sa_6_out, sa_7_out, sa_8_out;

  sa sa_1 (.A(B[7]), .B(A[7]), .IN(sa_2_out), .Diff(S[7]));  // open: OUT
  sa sa_2 (.A(B[6]), .B(A[6]), .IN(sa_3_out), .Diff(S[6]), .OUT(sa_2_out));
  sa sa_3 (.A(B[5]), .B(A[5]), .IN(sa_4_out), .Diff(S[5]), .OUT(sa_3_out));
  sa sa_4 (.A(B[4]), .B(A[4]), .IN(sa_5_out), .Diff(S[4]), .OUT(sa_4_out));
  sa sa_5 (.A(B[3]), .B(A[3]), .IN(sa_6_out), .Diff(S[3]), .OUT(sa_5_out));
  sa sa_6 (.A(B[2]), .B(A[2]), .IN(sa_7_out), .Diff(S[2]), .OUT(sa_6_out));
  sa sa_7 (.A(B[1]), .B(A[1]), .IN(sa_8_out), .Diff(S[1]), .OUT(sa_7_out));
  sa sa_8 (.A(B[0]), .B(A[0]), .IN(1'b0), .Diff(S[0]), .OUT(sa_8_out));
  // Pins of 4 and 8 bits meet at S
endmodule
