// Digital circuit sum.dig as structural Verilog
module sum (
  input  [7:0] A,
  input  [7:0] B,
  output [7:0] S
);

  wire fa_1_cout, fa_2_cout, fa_3_cout, fa_4_cout, fa_5_cout, fa_6_cout, fa_7_cout;

  fa fa_1 (.A(A[0]), .B(B[0]), .Cin(1'b0), .Cout(fa_1_cout), .S(S[0]));
  fa fa_2 (.A(A[1]), .B(B[1]), .Cin(fa_1_cout), .Cout(fa_2_cout), .S(S[1]));
  fa fa_3 (.A(A[2]), .B(B[2]), .Cin(fa_2_cout), .Cout(fa_3_cout), .S(S[2]));
  fa fa_4 (.A(A[3]), .B(B[3]), .Cin(fa_3_cout), .Cout(fa_4_cout), .S(S[3]));
  fa fa_5 (.A(A[4]), .B(B[4]), .Cin(fa_4_cout), .Cout(fa_5_cout), .S(S[4]));
  fa fa_6 (.A(A[5]), .B(B[5]), .Cin(fa_5_cout), .Cout(fa_6_cout), .S(S[5]));
  fa fa_7 (.A(A[6]), .B(B[6]), .Cin(fa_6_cout), .Cout(fa_7_cout), .S(S[6]));
  fa fa_8 (.A(A[7]), .B(B[7]), .Cin(fa_7_cout), .S(S[7]));  // open: Cout
  // Pins of 4 and 8 bits meet at S
  // Pins of 4 and 8 bits meet at A
  // Pins of 4 and 8 bits meet at B
endmodule
